# Fritzing sketch fritzing-diagram-comp-unwired (saved by Fritzing 1.0.4)
breadboards: 1

parts:
  Mod1 = ESP32-TTGO-T-DISPLAY
  S1 = Pushbutton [package="[THT]"]
  R1 = Flutesan Breadboard Trim-06 [package=THT]
  Part2 = Black Joystick KY-023

nets:
  N1: Mod1.G-1, Mod1.G-2, Mod1.G-10, Mod1.G-11, Mod1.G-14, S1.Pin_1, S1.Pin_2, R1.leg2, Part2.GND
  N2: Mod1.2, S1.Pin_3, S1.Pin_4
  N3: Mod1.13, R1.wiper
  N4: Mod1.3V, R1.leg1, Part2.+5V
  N5: Mod1.33, Part2.SW
  N6: Mod1.32, Part2.VRx
  N7: Mod1.39, Part2.VRy

custom parts:
  ESP32-TTGO-T-DISPLAY: LILYGO TTGO T-Display GD32VF103CBT6 Main Chip ST7789 1.14 Inch IPS 240x135 Resolution Minimalist Development Board.
  Flutesan Breadboard Trim-06: A rotary adjustable resistor (potentiometer) that is breadboard friendly and has a knob. Top view for perf board use.
  Black Joystick KY-023: Description: The joystick is a combination of 2 analoog potentiometer and a digital switch. Arduino GND --> Module pin - Arduino +5V --> Module pin +5V Arduino Analoog 0 --> Module VRx Arduino Analoog 1 --> Module VRy Arduino Digital --> Module SW Dimensions: 1" x 1.25"
